# Fritzing sketch Electric Schematics (saved by Fritzing 0.9.3b)
breadboards: 1

parts:
  Част1 = Arduino Uno (Rev3)
  LCD1 = LCD screen
  J1 = Piezo Speaker
  Част2 = SRF05 Ultrasonic Rangefinder
  S1 = Toggle Switch [package=THT]
  R1 = Resistor [tolerance=±5% resistance=220 package=THT]
  Част3 = SRF05 Ultrasonic Rangefinder

nets:
  N1: Част1.D8, Част2.Trig
  N2: Част1.D9_PWM, Част2.Echo
  N3: Част1.D10_PWM/SS, J1.pin2
  N4: Част1.D11_PWM/MOSI, LCD1.E
  N5: Част1.D12/MISO, LCD1.RS
  GND: Част1.GND, LCD1.VSS, LCD1.R/W, LCD1.LED-, J1.pin1, Част2.GND, S1.L2, Част3.GND
  N6: Част1.D2, LCD1.DB7
  N7: Част1.D3_PWM, LCD1.DB6
  N8: Част1.D4, LCD1.DB5
  N9: Част1.D5_PWM, LCD1.DB4
  N10: Част1.D6_PWM, Част3.Trig
  N11: Част1.D7, Част3.Echo
  VCC: Част1.5V, LCD1.VDD, Част2.VCC, S1.L1, R1.Pin_1, Част3.VCC
  N12: LCD1.V0, S1.COM
  N13: LCD1.LED+, R1.Pin_0
